// Logisim project ID_EX.circ as structural Verilog: 1 circuit, main circuit ID_EX
module ID_EX (
  input  clk,
  input  RegDstIn,
  input  BranchIn,
  input  JumpIn,
  input  RegWrEnIn,
  input  AluSrcIn,
  input  MemToRegIn,
  input  AluOprIn,
  input  [3:0] MemWrMaskIn,
  input  LBIn,
  input  [31:0] ReadData1In,
  input  [31:0] ReadData2In,
  input  [31:0] extendedBitsIn,
  input  [31:0] ExtendedIn,
  input  [4:0] ALu_outIn,
  input  sh_amountIn,
  input  [4:0] WrIdxIn,
  input  reset,
  output RegDstOut,
  output BranchOut,
  output JumpOut,
  output RegWrEnOut,
  output AluSrcOut,
  output MemToRegOut,
  output AluOprOut,
  output [3:0] MemWrMaskOut,
  output LBOut,
  output [31:0] ReadData1Out,
  output [31:0] ReadData2Out,
  output [31:0] extendedBitsOut,
  output [31:0] ExtendedOut,
  output [4:0] Alu_outOut,
  output sh_amountOut,
  output [4:0] WrIdxOut
);

  Register #(.width(1)) register_1 (.D(RegDstIn), .clk(clk), .Q(RegDstOut), .clr(reset));  // open: en
  Register #(.width(1)) register_2 (.D(BranchIn), .clk(clk), .Q(BranchOut), .clr(reset));  // open: en
  Register #(.width(1)) register_3 (.D(JumpIn), .clk(clk), .Q(JumpOut), .clr(reset));  // open: en
  Register #(.width(1)) register_4 (.D(RegWrEnIn), .clk(clk), .Q(RegWrEnOut), .clr(reset));  // open: en
  Register #(.width(1)) register_5 (.D(AluSrcIn), .clk(clk), .Q(AluSrcOut), .clr(reset));  // open: en
  Register #(.width(1)) register_6 (.D(MemToRegIn), .clk(clk), .Q(MemToRegOut), .clr(reset));  // open: en
  Register #(.width(1)) register_7 (.D(AluOprIn), .clk(clk), .Q(AluOprOut), .clr(reset));  // open: en
  Register #(.width(4)) register_8 (.D(MemWrMaskIn), .clk(clk), .Q(MemWrMaskOut), .clr(reset));  // open: en
  Register #(.width(1)) register_9 (.D(LBIn), .clk(clk), .Q(LBOut), .clr(reset));  // open: en
  Register #(.width(32)) register_10 (.D(ReadData1In), .clk(clk), .Q(ReadData1Out), .clr(reset));  // open: en
  Register #(.width(32)) register_11 (.D(ReadData2In), .clk(clk), .Q(ReadData2Out), .clr(reset));  // open: en
  Register #(.width(32)) register_12 (.D(extendedBitsIn), .clk(clk), .Q(extendedBitsOut), .clr(reset));  // open: en
  Register #(.width(32)) register_13 (.D(ExtendedIn), .clk(clk), .Q(ExtendedOut), .clr(reset));  // open: en
  Register #(.width(5)) register_14 (.D(ALu_outIn), .clk(clk), .Q(Alu_outOut), .clr(reset));  // open: en
  Register #(.width(1)) register_15 (.D(sh_amountIn), .clk(clk), .Q(sh_amountOut), .clr(reset));  // open: en
  Register #(.width(5)) register_16 (.D(WrIdxIn), .clk(clk), .Q(WrIdxOut), .clr(reset));  // open: en
endmodule
