// Logisim project alu.circ as structural Verilog: 1 circuit, main circuit ALU
module ALU (
  input  [31:0] ReadData1,
  input  [31:0] ReadData2,
  input  [4:0] ControlBits,
  output [31:0] Result,
  output Zero
);

  wire comparator_1_lt;
  wire [4:0] xor_1_out, xor_2_out;
  wire [31:0] I0, I1, I2, I3, I4, I7, I8, I9, I10, I11, I12, I13, I14, I15, I16, I17, undriven;

  Shifter #(.width(32)) shifter_1 (.in(ReadData2), .\dist (ReadData1[4:0]), .out(I0));
  Shifter #(.shift("lr"), .width(32)) shifter_2 (.in(ReadData2), .\dist (ReadData1[4:0]), .out(I1));
  Shifter #(.shift("ar"), .width(32)) shifter_3 (.in(ReadData2), .\dist (ReadData1[4:0]), .out(I2));
  Shifter #(.width(32)) shifter_4 (.in(ReadData2), .\dist (ReadData1[4:0]), .out(I3));
  Shifter #(.shift("lr"), .width(32)) shifter_5 (.in(ReadData2), .\dist (ReadData1[4:0]), .out(I4));
  assign xor_1_out = ControlBits ^ 5'b00101;  // XOR_Gate xor_1, 5 bits wide
  assign xor_2_out = ControlBits ^ 5'b00110;  // XOR_Gate xor_2, 5 bits wide
  Multiplier #(.mode("twosComplement"), .width(32)) multiplier_1 (
    .a(ReadData1), .b(ReadData2), .out(I7));  // open: cin, cout
  Divider #(.mode("twosComplement"), .width(32)) divider_1 (
    .a(ReadData1), .b(ReadData2), .out(I8));  // open: upper, rem
  Adder #(.width(32)) adder_1 (.a(ReadData1), .b(ReadData2), .out(I9));  // open: cin, cout
  Adder #(.width(32)) adder_2 (.a(ReadData1), .b(ReadData2), .out(I10));  // open: cin, cout
  Subtractor #(.width(32)) subtractor_1 (.a(ReadData1), .b(ReadData2), .out(I11));  // open: bin, bout
  Subtractor #(.width(32)) subtractor_2 (.a(ReadData1), .b(ReadData2), .out(I12));  // open: bin, bout
  assign I13 = ReadData1 & ReadData2;  // AND_Gate and_1, 32 bits wide
  assign I14 = ReadData1 | ReadData2;  // OR_Gate or_1, 32 bits wide
  assign I15 = ReadData1 ^ ReadData2;  // XOR_Gate xor_3, 32 bits wide
  nor nor_1 (Zero, xor_1_out[0], xor_1_out[1], xor_1_out[2], xor_1_out[3], xor_1_out[4]);
  nor nor_2 (Zero, xor_2_out[0], xor_2_out[1], xor_2_out[2], xor_2_out[3], xor_2_out[4]);
  assign I16 = ~(ReadData1 | ReadData2);  // NOR_Gate nor_3, 32 bits wide
  Comparator #(.width(32)) comparator_1 (.a(ReadData1), .b(ReadData2), .lt(comparator_1_lt));  // open: gt, eq
  assign I17 = {{31{1'b0}}, comparator_1_lt};  // Bit_Extender bit_extender_1
  Multiplexer #(.enable("true"), .select(5), .width(32)) multiplexer_1 (
    .in0(I0), .in1(I1), .in2(I2), .in3(I3), .in4(I4), .in5(ReadData1), .in6({32{1'b1}}), .in7(I7), .in8(I8),
    .in9(I9), .in10(I10), .in11(I11), .in12(I12), .in13(I13), .in14(I14), .in15(I15), .in16(I16), .in17(I17),
    .in31(undriven), .out(Result), .sel(ControlBits));  // open: in18, in19, in20, in21, in22, in23, in24, in25, in26, in27, in28, in29, in30, en

  // Other names for the same wires on the sheet: I5[31:0] = ReadData1

  // Notes on the sheet:
  //   use an AND gate after adding the other types!
  //   signed?
  //   unsigned?
  //   syscall
endmodule
