// Logisim project cache.circ as structural Verilog: 1 circuit, main circuit Cache
module Cache (
  input  clk,
  input  [31:0] WriteData,
  input  [31:0] Address,
  input  WriteEnable,
  output [31:0] ReadData,
  output HIT,
  output [31:0] AddressOut,
  output WriteInMemory,
  output [31:0] WriteDataOut
);

  wire and_2_out, and_3_out, and_4_out, and_5_out, and_6_out, and_7_out, and_8_out, and_9_out, and_10_out,
       and_11_out, and_12_out, and_13_out, and_23_out, and_24_out, and_33_out, and_34_out, C0, C1, C2, C3,
       comparator_2_eq, comparator_4_eq, comparator_6_eq, comparator_8_eq, or_1_out, or_2_out, or_3_out,
       or_4_out, Select_0, Select_1, Select_2, Select_3, Set0, Set1, Set2, Set3, V0, V1, V2, V3, V4, V5, V6,
       V7, WE0, WE1, WE2, WE3, WE4, WE5, WE6, WE7, WE8, WE9, WE10, WE11, WE12, WE13, WE14, WE15, WE16, WE17,
       WE18, WE19, WE20, WE21, WE22, WE23, WE24, WE25, WE26, WE27, WE28, WE29, WE30, WE31, WH, Word0, Word1,
       Word2, Word3;
  wire [1:0] adder_4_out, register_53_q;
  wire [9:0] T0, T1, T2, T3, T4, T5, T6, T7;
  wire [31:0] adder_1_out, adder_2_out, adder_3_out, and_1_out, multiplexer_1_out, multiplexer_2_out,
       multiplexer_3_out, multiplexer_4_out, multiplexer_5_out, multiplexer_6_out, multiplexer_7_out,
       multiplexer_8_out, multiplexer_9_out, multiplexer_10_out, multiplexer_11_out, multiplexer_12_out, W0,
       W1, W2, W3, W4, W5, W6, W7, W8, W9, W10, W11, W12, W13, W14, W15, W16, W17, W18, W19, W20, W21, W22,
       W23, W24, W25, W26, W27, W28, W29, W30, W31;

  Register #(.width(1)) register_1 (.Q(C0));  // open: D, en, clk, clr
  Register #(.width(1)) register_2 (.Q(C1));  // open: D, en, clk, clr
  Register #(.width(1)) register_3 (.Q(C2));  // open: D, en, clk, clr
  Register #(.width(1)) register_4 (.Q(C3));  // open: D, en, clk, clr
  Decoder #(.select(2)) decoder_1 (.out0(Set0), .out1(Set1), .out2(Set2), .out3(Set3), .sel(Address[5:4]));  // open: en
  Decoder #(.select(2)) decoder_2 (
    .out0(Word0), .out1(Word1), .out2(Word2), .out3(Word3), .sel(Address[3:2]));  // open: en
  Register #(.width(1)) register_5 (.Q(V0));  // open: D, en, clk, clr
  Register #(.width(1)) register_6 (.Q(V1));  // open: D, en, clk, clr
  Register #(.width(1)) register_7 (.Q(V2));  // open: D, en, clk, clr
  Register #(.width(1)) register_8 (.Q(V3));  // open: D, en, clk, clr
  Register #(.width(1)) register_9 (.Q(V4));  // open: D, en, clk, clr
  Register #(.width(1)) register_10 (.Q(V5));  // open: D, en, clk, clr
  Register #(.width(1)) register_11 (.Q(V6));  // open: D, en, clk, clr
  Register #(.width(1)) register_12 (.Q(V7));  // open: D, en, clk, clr
  Register #(.width(10)) register_13 (.Q(T0));  // open: D, en, clk, clr
  Register #(.width(10)) register_14 (.Q(T1));  // open: D, en, clk, clr
  Register #(.width(10)) register_15 (.Q(T2));  // open: D, en, clk, clr
  Register #(.width(10)) register_16 (.Q(T3));  // open: D, en, clk, clr
  Register #(.width(10)) register_17 (.Q(T4));  // open: D, en, clk, clr
  Register #(.width(10)) register_18 (.Q(T5));  // open: D, en, clk, clr
  Register #(.width(10)) register_19 (.Q(T6));  // open: D, en, clk, clr
  Register #(.width(10)) register_20 (.Q(T7));  // open: D, en, clk, clr
  Register #(.width(32)) register_21 (.D(WriteData), .en(WE0), .clk(clk), .Q(W0));  // open: clr
  Register #(.width(32)) register_22 (.D(WriteData), .en(WE4), .clk(clk), .Q(W4));  // open: clr
  Register #(.width(32)) register_23 (.D(WriteData), .en(WE8), .clk(clk), .Q(W8));  // open: clr
  Register #(.width(32)) register_24 (.D(WriteData), .en(WE12), .clk(clk), .Q(W12));  // open: clr
  Register #(.width(32)) register_25 (.D(WriteData), .en(WE16), .clk(clk), .Q(W16));  // open: clr
  Register #(.width(32)) register_26 (.D(WriteData), .en(WE20), .clk(clk), .Q(W20));  // open: clr
  Register #(.width(32)) register_27 (.D(WriteData), .en(WE24), .clk(clk), .Q(W24));  // open: clr
  Register #(.width(32)) register_28 (.D(WriteData), .en(WE28), .clk(clk), .Q(W28));  // open: clr
  Register #(.width(32)) register_29 (.D(WriteData), .en(WE1), .clk(clk), .Q(W1));  // open: clr
  Register #(.width(32)) register_30 (.D(WriteData), .en(WE5), .clk(clk), .Q(W5));  // open: clr
  Register #(.width(32)) register_31 (.D(WriteData), .en(WE9), .clk(clk), .Q(W9));  // open: clr
  Register #(.width(32)) register_32 (.D(WriteData), .en(WE13), .clk(clk), .Q(W13));  // open: clr
  Register #(.width(32)) register_33 (.D(WriteData), .en(WE17), .clk(clk), .Q(W17));  // open: clr
  Register #(.width(32)) register_34 (.D(WriteData), .en(WE21), .clk(clk), .Q(W21));  // open: clr
  Register #(.width(32)) register_35 (.D(WriteData), .en(WE25), .clk(clk), .Q(W25));  // open: clr
  Register #(.width(32)) register_36 (.D(WriteData), .en(WE29), .clk(clk), .Q(W29));  // open: clr
  Register #(.width(32)) register_37 (.D(WriteData), .en(WE2), .clk(clk), .Q(W2));  // open: clr
  Register #(.width(32)) register_38 (.D(WriteData), .en(WE6), .clk(clk), .Q(W6));  // open: clr
  Register #(.width(32)) register_39 (.D(WriteData), .en(WE10), .clk(clk), .Q(W10));  // open: clr
  Register #(.width(32)) register_40 (.D(WriteData), .en(WE14), .clk(clk), .Q(W14));  // open: clr
  Register #(.width(32)) register_41 (.D(WriteData), .en(WE18), .clk(clk), .Q(W18));  // open: clr
  Register #(.width(32)) register_42 (.D(WriteData), .en(WE22), .clk(clk), .Q(W22));  // open: clr
  Register #(.width(32)) register_43 (.D(WriteData), .en(WE26), .clk(clk), .Q(W26));  // open: clr
  Register #(.width(32)) register_44 (.D(WriteData), .en(WE30), .clk(clk), .Q(W30));  // open: clr
  Register #(.width(32)) register_45 (.D(WriteData), .en(WE3), .clk(clk), .Q(W3));  // open: clr
  Register #(.width(32)) register_46 (.D(WriteData), .en(WE7), .clk(clk), .Q(W7));  // open: clr
  Register #(.width(32)) register_47 (.D(WriteData), .en(WE11), .clk(clk), .Q(W11));  // open: clr
  Register #(.width(32)) register_48 (.D(WriteData), .en(WE15), .clk(clk), .Q(W15));  // open: clr
  Register #(.width(32)) register_49 (.D(WriteData), .en(WE19), .clk(clk), .Q(W19));  // open: clr
  Register #(.width(32)) register_50 (.D(WriteData), .en(WE23), .clk(clk), .Q(W23));  // open: clr
  Register #(.width(32)) register_51 (.D(WriteData), .en(WE27), .clk(clk), .Q(W27));  // open: clr
  Register #(.width(32)) register_52 (.D(WriteData), .en(WE31), .clk(clk), .Q(W31));  // open: clr
  Multiplexer #(.select(2), .width(32)) multiplexer_1 (
    .in0(W0), .in1(W1), .in2(W2), .in3(W3), .out(multiplexer_1_out), .sel(Address[3:2]));
  Multiplexer #(.select(2), .width(32)) multiplexer_2 (
    .in0(W4), .in1(W5), .in2(W6), .in3(W7), .out(multiplexer_2_out), .sel(Address[3:2]));
  Multiplexer #(.select(2), .width(32)) multiplexer_3 (
    .in0(W8), .in1(W9), .in2(W10), .in3(W11), .out(multiplexer_3_out), .sel(Address[3:2]));
  Multiplexer #(.select(2), .width(32)) multiplexer_4 (
    .in0(W12), .in1(W13), .in2(W14), .in3(W15), .out(multiplexer_4_out), .sel(Address[3:2]));
  Multiplexer #(.select(2), .width(32)) multiplexer_5 (
    .in0(W16), .in1(W17), .in2(W18), .in3(W19), .out(multiplexer_5_out), .sel(Address[3:2]));
  Multiplexer #(.select(2), .width(32)) multiplexer_6 (
    .in0(W20), .in1(W21), .in2(W22), .in3(W23), .out(multiplexer_6_out), .sel(Address[3:2]));
  Multiplexer #(.select(2), .width(32)) multiplexer_7 (
    .in0(W24), .in1(W25), .in2(W26), .in3(W27), .out(multiplexer_7_out), .sel(Address[3:2]));
  Multiplexer #(.select(2), .width(32)) multiplexer_8 (
    .in0(W28), .in1(W29), .in2(W30), .in3(W31), .out(multiplexer_8_out), .sel(Address[3:2]));
  Multiplexer #(.width(32)) multiplexer_9 (
    .in0(multiplexer_1_out), .in1(multiplexer_2_out), .out(multiplexer_9_out), .sel(Select_0));
  Multiplexer #(.width(32)) multiplexer_10 (
    .in0(multiplexer_3_out), .in1(multiplexer_4_out), .out(multiplexer_10_out), .sel(Select_1));
  Multiplexer #(.width(32)) multiplexer_11 (
    .in0(multiplexer_5_out), .in1(multiplexer_6_out), .out(multiplexer_11_out), .sel(Select_2));
  Multiplexer #(.width(32)) multiplexer_12 (
    .in0(multiplexer_7_out), .in1(multiplexer_8_out), .out(multiplexer_12_out), .sel(Select_3));
  Multiplexer #(.select(2), .width(32)) multiplexer_13 (
    .in0(multiplexer_9_out), .in1(multiplexer_10_out), .in2(multiplexer_11_out), .in3(multiplexer_12_out),
    .out(ReadData), .sel(Address[5:4]));
  Comparator #(.width(10)) comparator_1 (.a(T1), .b(Address[15:6]), .eq(Select_0));  // open: gt, lt
  Comparator #(.width(10)) comparator_2 (.a(T0), .b(Address[15:6]), .eq(comparator_2_eq));  // open: gt, lt
  assign and_1_out = Address & 32'hfffffff3;  // AND_Gate and_1, 32 bits wide
  and and_2 (and_2_out, V1, Select_0);
  and and_3 (and_3_out, V0, comparator_2_eq);
  Adder #(.width(32)) adder_1 (.a(and_1_out), .b(32'h4), .out(adder_1_out));  // open: cin, cout
  Adder #(.width(32)) adder_2 (.a(and_1_out), .b(32'h8), .out(adder_2_out));  // open: cin, cout
  Adder #(.width(32)) adder_3 (.a(and_1_out), .b(32'hc), .out(adder_3_out));  // open: cin, cout
  or or_1 (or_1_out, and_2_out, and_3_out);
  Register #(.width(2)) register_53 (.D(adder_4_out), .clk(clk), .Q(register_53_q));  // open: en, clr
  Multiplexer #(.select(2), .width(32)) multiplexer_14 (
    .in0(and_1_out), .in1(adder_1_out), .in2(adder_2_out), .in3(adder_3_out), .out(AddressOut),
    .sel(register_53_q));
  Comparator #(.width(10)) comparator_3 (.a(T3), .b(Address[15:6]), .eq(Select_1));  // open: gt, lt
  Comparator #(.width(10)) comparator_4 (.a(T2), .b(Address[15:6]), .eq(comparator_4_eq));  // open: gt, lt
  Adder #(.width(2)) adder_4 (.a(register_53_q), .b(2'b01), .out(adder_4_out));  // open: cin, cout
  and and_4 (and_4_out, V3, Select_1);
  and and_5 (and_5_out, V2, comparator_4_eq);
  Multiplexer #(.select(2)) multiplexer_15 (
    .in0(or_1_out), .in1(or_2_out), .in2(or_3_out), .in3(or_4_out), .out(HIT), .sel(Address[5:4]));
  or or_2 (or_2_out, and_4_out, and_5_out);
  and and_6 (and_6_out, ~Select_0, Set0, WH);  // AND_Gate
  and and_7 (and_7_out, Select_0, Set0, WH);
  and and_8 (and_8_out, ~Select_1, Set1, WH);  // AND_Gate
  and and_9 (and_9_out, Select_1, Set1, WH);
  and and_10 (and_10_out, ~Select_2, Set2, WH);  // AND_Gate
  and and_11 (and_11_out, Select_2, Set2, WH);
  and and_12 (and_12_out, ~Select_3, Set3, WH);  // AND_Gate
  and and_13 (and_13_out, Select_3, Set3, WH);
  Comparator #(.width(10)) comparator_5 (.a(T5), .b(Address[15:6]), .eq(Select_2));  // open: gt, lt
  Comparator #(.width(10)) comparator_6 (.a(T4), .b(Address[15:6]), .eq(comparator_6_eq));  // open: gt, lt
  and and_14 (WH, WriteEnable, HIT);
  and and_15 (WE0, Word0, and_6_out);
  and and_16 (WE4, Word0, and_7_out);
  and and_17 (WE8, Word0, and_8_out);
  and and_18 (WE12, Word0, and_9_out);
  and and_19 (WE16, Word0, and_10_out);
  and and_20 (WE20, Word0, and_11_out);
  and and_21 (WE24, Word0, and_12_out);
  and and_22 (WE28, Word0, and_13_out);
  and and_23 (and_23_out, V5, Select_2);
  or or_3 (or_3_out, and_23_out, and_24_out);
  and and_24 (and_24_out, V4, comparator_6_eq);
  and and_25 (WE1, Word1, and_6_out);
  and and_26 (WE5, Word1, and_7_out);
  and and_27 (WE9, Word1, and_8_out);
  and and_28 (WE13, Word1, and_9_out);
  and and_29 (WE17, Word1, and_10_out);
  and and_30 (WE21, Word1, and_11_out);
  and and_31 (WE25, Word1, and_12_out);
  and and_32 (WE29, Word1, and_13_out);
  Comparator #(.width(10)) comparator_7 (.a(T7), .b(Address[15:6]), .eq(Select_3));  // open: gt, lt
  Comparator #(.width(10)) comparator_8 (.a(T6), .b(Address[15:6]), .eq(comparator_8_eq));  // open: gt, lt
  and and_33 (and_33_out, V7, Select_3);
  and and_34 (and_34_out, V6, comparator_8_eq);
  and and_35 (WE2, Word2, and_6_out);
  and and_36 (WE6, Word2, and_7_out);
  and and_37 (WE10, Word2, and_8_out);
  and and_38 (WE14, Word2, and_9_out);
  and and_39 (WE18, Word2, and_10_out);
  and and_40 (WE22, Word2, and_11_out);
  and and_41 (WE26, Word2, and_12_out);
  and and_42 (WE30, Word2, and_13_out);
  or or_4 (or_4_out, and_33_out, and_34_out);
  and and_43 (WE3, Word3, and_6_out);
  and and_44 (WE7, Word3, and_7_out);
  and and_45 (WE11, Word3, and_8_out);
  and and_46 (WE15, Word3, and_9_out);
  and and_47 (WE19, Word3, and_10_out);
  and and_48 (WE23, Word3, and_11_out);
  and and_49 (WE27, Word3, and_12_out);
  and and_50 (WE31, Word3, and_13_out);

  // Other names for the same wires on the sheet: word[1:0] = Address[3:2]; Set[1:0] = Address[5:4];
  //   Tag[9:0] = Address[15:6]; Clock = clk

  // Notes on the sheet:
  //   Inja ride:
endmodule
