// Logisim project cpu.circ as structural Verilog: 1 circuit, main circuit cpu
module cpu (
  input  Rest
);

  wire alu_1_zero, alucontroller_1_sh_amount, and_1_out, and_2_out, and_3_out, and_6_out, and_7_out, AO, BR,
       BR_EXMEM, CAcc, CAcc_EXMEM, CAcc_IDEX, cache_1_hit, cache_1_last_we, cache_1_readfrommem,
       cache_1_writeinmemory, clk, comparator_1_eq, comparator_2_eq, comparator_3_eq, controller_1_alusrc,
       controller_1_branch, controller_1_jump, controller_1_lb, controller_1_memtoreg, controller_1_regdst,
       controller_1_regwren, ex_mem_1_p22, ex_mem_1_p23, ex_mem_1_p24, FRZ, id_ex_1_alusrcout,
       id_ex_1_sh_amountout, JO, JR_EXMEM, JR_WB, Jump_EXMEM, Jump_WB, LB, memToReg, MTR, multiplexer_1_out,
       multiplexer_3_out, not_1_out, not_2_out, or_1_out, or_2_out, RD, RegDst_WB, RegWrEn_WB, RType, RType2,
       RW, Syscall_EXMEM, Syscall_WB, Zero_EXMEM;
  wire [1:0] alu_1_result, undriven;
  wire [3:0] bit_extender_5_out, controller_1_memwrmask, ex_mem_1_p25, id_ex_1_memwrmaskout,
       multiplexer_10_out, oneclockdelay_1_dataout_2, shifter_4_out;
  wire [4:0] alucontroller_1_alu_out, bit_extender_4_out, ex_mem_1_p26, id_ex_1_alu_outout,
       multiplexer_6_out, oneclockdelay_2_dataout_2, oneclockdelay_2_dataout_3, shifter_5_out, WrIdx,
       WrIdx_IDEX, WrIdx_WB;
  wire [5:0] oneclockdelay_2_dataout;
  wire [7:0] multiplexer_16_out;
  wire [25:16] oneclockdelay_2_dataout_4;
  wire [27:0] oneclockdelay_1_dataout;
  wire [31:0] adder_1_out, adder_2_out, AluRes_EXMEM, AluRes_WB, bit_extender_1_out, bit_extender_2_out,
       bit_extender_3_out, bit_extender_6_out, cache_1_addressout, cache_1_last_w_data, cache_1_readdata,
       cache_1_writedataout, ex_mem_1_p17, ex_mem_pc_1_br_pcout, ex_mem_pc_1_j_pcout, ex_mem_pc_1_pcout,
       id_ex_1_extendedbitsout, id_ex_1_extendedout, id_ex_1_readdata1out, id_ex_1_readdata2out,
       id_ex_pc_1_j_pcout, id_ex_pc_1_pcout, mem_1_memreaddata, mem_wb_1_cachereadout, MemData,
       multiplexer_2_out, multiplexer_4_out, multiplexer_7_out, multiplexer_8_out, multiplexer_9_out,
       multiplexer_11_out, multiplexer_12_out, multiplexer_13_out, multiplexer_14_out, multiplexer_17_out,
       multiplexer_18_out, PC_EXMEM, PC_q, PC_WB, regfile_1_p7, regfile_1_p8, shifter_1_out, shifter_2_out,
       shifter_3_out, shifter_6_out, signextend_1_extended, undriven_2, xor_1_out;
  wire [31:2] alu_1_result_2;
  wire [31:26] oneclockdelay_2_dataout_5;

  Multiplexer multiplexer_1 (.in0(1'b1), .in1(1'b0), .out(multiplexer_1_out), .sel(Syscall_WB));
  Multiplexer #(.width(32)) multiplexer_2 (
    .in0(multiplexer_4_out), .in1(AluRes_WB), .out(multiplexer_2_out), .sel(JR_WB));
  Register #(.width(32)) PC (.D(multiplexer_2_out), .en(multiplexer_3_out), .clk(clk), .Q(PC_q), .clr(Rest));
  Multiplexer multiplexer_3 (.in0(multiplexer_1_out), .in1(1'b0), .out(multiplexer_3_out), .sel(FRZ));
  Clock u_Clk (.out(clk));
  or or_1 (or_1_out, Jump_EXMEM, and_1_out);
  Multiplexer #(.width(32)) multiplexer_4 (.in0(adder_1_out), .in1(PC_EXMEM), .out(multiplexer_4_out), .sel(or_1_out));
  Adder #(.width(32)) adder_1 (.a(32'h4), .b(PC_q), .out(adder_1_out));  // open: cin, cout
  mem mem_1 (.MemAddress(PC_q), .clk(clk), .MemReadData(mem_1_memreaddata));  // open: MemWriteMask, MemWriteData
  and and_1 (and_1_out, BR_EXMEM, Zero_EXMEM);
  oneClockDelay oneclockdelay_1 (
    .DataIn(adder_1_out), .clk(clk), .Freeze(FRZ),
    .DataOut({oneclockdelay_1_dataout_2, oneclockdelay_1_dataout}));
  oneClockDelay oneclockdelay_2 (
    .DataIn(mem_1_memreaddata), .clk(clk), .Freeze(FRZ),
    .DataOut({oneclockdelay_2_dataout_5, oneclockdelay_2_dataout_4, oneclockdelay_2_dataout_3, oneclockdelay_2_dataout_2, oneclockdelay_2_dataout}));
  Multiplexer #(.width(5)) multiplexer_5 (
    .in0(oneclockdelay_2_dataout_4[20:16]), .in1(oneclockdelay_2_dataout_3), .out(WrIdx),
    .sel(controller_1_regdst));
  assign bit_extender_1_out = {{6{1'b0}}, {oneclockdelay_2_dataout_4, oneclockdelay_2_dataout_3, oneclockdelay_2_dataout_2, oneclockdelay_2_dataout}};  // Bit_Extender bit_extender_1
  and and_2 (and_2_out, Jump_WB, RegWrEn_WB);
  Multiplexer #(.width(5)) multiplexer_6 (.in0(WrIdx_WB), .in1({5{1'b1}}), .out(multiplexer_6_out), .sel(and_2_out));
  Multiplexer #(.width(32)) multiplexer_7 (
    .in0(multiplexer_18_out), .in1(PC_WB), .out(multiplexer_7_out), .sel(and_2_out));
  Shifter #(.width(32)) shifter_1 (.in(bit_extender_1_out), .\dist (5'b00010), .out(shifter_1_out));
  assign bit_extender_2_out = {{28{1'b0}}, oneclockdelay_1_dataout_2};  // Bit_Extender bit_extender_2
  assign bit_extender_3_out = {{27{1'b0}}, oneclockdelay_2_dataout_2};  // Bit_Extender bit_extender_3
  Shifter #(.width(32)) shifter_2 (.in(bit_extender_2_out), .\dist (5'b11100), .out(shifter_2_out));
  Controller controller_1 (
    .Opcode(oneclockdelay_2_dataout_5), .RegDst(controller_1_regdst), .Branch(controller_1_branch),
    .Jump(controller_1_jump), .RegWrEn(controller_1_regwren), .AluSrc(controller_1_alusrc),
    .MemToReg(controller_1_memtoreg), .AluOpr(AO), .MemWrMask(controller_1_memwrmask), .LB(controller_1_lb),
    .CacheAcc(CAcc));
  assign xor_1_out = shifter_1_out ^ shifter_2_out;  // XOR_Gate xor_1, 32 bits wide
  // regfile regfile_1: pin names not known; wires that end beside it: oneclockdelay_2_dataout_4[25:21], oneclockdelay_2_dataout_4[20:16], multiplexer_6_out, multiplexer_7_out, RegWrEn_WB, clk, regfile_1_p7, regfile_1_p8
  signExtend signextend_1 (
    .Immd({oneclockdelay_2_dataout_3, oneclockdelay_2_dataout_2, oneclockdelay_2_dataout}),
    .Extended(signextend_1_extended));
  AluController alucontroller_1 (
    .func(oneclockdelay_2_dataout), .opcode(oneclockdelay_2_dataout_5), .aluOperation(AO),
    .ALU_out(alucontroller_1_alu_out), .sh_amount(alucontroller_1_sh_amount));
  ID_EX_PC id_ex_pc_1 (
    .Clock(clk), .J_PCIN(xor_1_out), .PCIn({oneclockdelay_1_dataout_2, oneclockdelay_1_dataout}),
    .reset(FRZ), .J_PCOUT(id_ex_pc_1_j_pcout), .PCOut(id_ex_pc_1_pcout));
  ID_EX id_ex_1 (
    .clk(clk), .RegDstIn(controller_1_regdst), .BranchIn(controller_1_branch), .JumpIn(controller_1_jump),
    .RegWrEnIn(controller_1_regwren), .AluSrcIn(controller_1_alusrc), .MemToRegIn(controller_1_memtoreg),
    .AluOprIn(AO), .MemWrMaskIn(controller_1_memwrmask), .LBIn(controller_1_lb), .ReadData1In(regfile_1_p7),
    .ReadData2In(regfile_1_p8), .extendedBitsIn(bit_extender_3_out), .ExtendedIn(signextend_1_extended),
    .ALu_outIn(alucontroller_1_alu_out), .sh_amountIn(alucontroller_1_sh_amount), .WrIdxIn(WrIdx),
    .CAccIn(CAcc), .Freeze(FRZ), .RegDstOut(RD), .BranchOut(BR), .JumpOut(JO), .RegWrEnOut(RW),
    .AluSrcOut(id_ex_1_alusrcout), .MemToRegOut(MTR), .AluOprOut(RType), .MemWrMaskOut(id_ex_1_memwrmaskout),
    .LBOut(LB), .ReadData1Out(id_ex_1_readdata1out), .ReadData2Out(id_ex_1_readdata2out),
    .extendedBitsOut(id_ex_1_extendedbitsout), .ExtendedOut(id_ex_1_extendedout),
    .Alu_outOut(id_ex_1_alu_outout), .sh_amountOut(id_ex_1_sh_amountout), .WrIdxOut(WrIdx_IDEX),
    .CAccOut(CAcc_IDEX));
  and and_3 (and_3_out, ~BR, id_ex_1_alusrcout);  // AND_Gate
  Multiplexer #(.width(32)) multiplexer_8 (
    .in0(id_ex_1_readdata1out), .in1(id_ex_1_extendedbitsout), .out(multiplexer_8_out),
    .sel(id_ex_1_sh_amountout));
  Shifter #(.width(32)) shifter_3 (.in(id_ex_1_extendedout), .\dist (5'b00010), .out(shifter_3_out));
  Multiplexer #(.width(32)) multiplexer_9 (
    .in0(id_ex_1_readdata2out), .in1(id_ex_1_extendedout), .out(multiplexer_9_out), .sel(and_3_out));
  assign bit_extender_4_out = {{3{1'b0}}, alu_1_result};  // Bit_Extender bit_extender_4
  Adder #(.width(32)) adder_2 (.a(id_ex_pc_1_pcout), .b(shifter_3_out), .out(adder_2_out));  // open: cin, cout
  Comparator #(.width(4)) comparator_1 (.a(id_ex_1_memwrmaskout), .b(4'b0001), .eq(comparator_1_eq));  // open: gt, lt
  Shifter #(.width(4)) shifter_4 (.in(id_ex_1_memwrmaskout), .\dist (alu_1_result), .out(shifter_4_out));
  Shifter #(.width(5)) shifter_5 (.in(bit_extender_4_out), .\dist (3'b011), .out(shifter_5_out));
  Shifter #(.width(32)) shifter_6 (.in(id_ex_1_readdata2out), .\dist (shifter_5_out), .out(shifter_6_out));
  Multiplexer #(.width(4)) multiplexer_10 (
    .in0(id_ex_1_memwrmaskout), .in1(shifter_4_out), .out(multiplexer_10_out), .sel(comparator_1_eq));
  ALU alu_1 (
    .ReadData1(multiplexer_8_out), .ReadData2(multiplexer_9_out), .ControlBits(id_ex_1_alu_outout),
    .Result({alu_1_result_2, alu_1_result}), .Zero(alu_1_zero));
  Multiplexer #(.width(32)) multiplexer_11 (
    .in0(id_ex_1_readdata2out), .in1(shifter_6_out), .out(multiplexer_11_out), .sel(comparator_1_eq));
  EX_MEM_PC ex_mem_pc_1 (
    .Clock(clk), .J_PCIN(id_ex_pc_1_j_pcout), .PCIN(id_ex_pc_1_pcout), .BR_PCIN(adder_2_out), .Freeze(FRZ),
    .J_PCOUT(ex_mem_pc_1_j_pcout), .PCOUT(ex_mem_pc_1_pcout), .BR_PCOUT(ex_mem_pc_1_br_pcout));
  // EX_MEM ex_mem_1: pin names not known; wires that end beside it: clk, {alu_1_result_2, alu_1_result}, multiplexer_11_out, alu_1_zero, BR, RType, JO, MTR, RD, RW, multiplexer_10_out, LB, WrIdx_IDEX, CAcc_IDEX, FRZ, AluRes_EXMEM, ex_mem_1_p17, Zero_EXMEM, BR_EXMEM, RType2, Jump_EXMEM, ex_mem_1_p22, ex_mem_1_p23, ex_mem_1_p24, ex_mem_1_p25, ex_mem_1_p26, CAcc_EXMEM
  and and_4 (JR_EXMEM, Zero_EXMEM, ~comparator_3_eq, RType2);  // AND_Gate
  and and_5 (Syscall_EXMEM, RType2, Zero_EXMEM, comparator_3_eq);
  Multiplexer #(.width(32)) multiplexer_12 (
    .in0(MemData), .in1(AluRes_EXMEM), .out(multiplexer_12_out), .sel(cache_1_readfrommem));
  Comparator #(.width(4)) comparator_2 (.a(4'b1111), .b(ex_mem_1_p25), .eq(comparator_2_eq));  // open: gt, lt
  Multiplexer #(.width(32)) multiplexer_13 (
    .in0(ex_mem_pc_1_pcout), .in1(ex_mem_pc_1_br_pcout), .out(multiplexer_13_out), .sel(and_6_out));
  and and_6 (and_6_out, BR_EXMEM, Zero_EXMEM);
  Multiplexer #(.width(32)) multiplexer_14 (
    .in0(multiplexer_12_out), .in1(cache_1_last_w_data), .out(multiplexer_14_out), .sel(cache_1_last_we));
  Multiplexer #(.width(32)) multiplexer_15 (
    .in0(ex_mem_pc_1_j_pcout), .in1(multiplexer_13_out), .out(PC_EXMEM), .sel(not_1_out));
  not not_1 (not_1_out, Jump_EXMEM);
  Comparator #(.width(32)) comparator_3 (.a(AluRes_EXMEM), .b({32{1'b1}}), .eq(comparator_3_eq));  // open: gt, lt
  or or_2 (or_2_out, cache_1_readfrommem, cache_1_last_we, comparator_2_eq);
  assign bit_extender_5_out = {{3{cache_1_writeinmemory}}, cache_1_writeinmemory};  // Bit_Extender bit_extender_5
  Cache cache_1 (
    .clk(clk), .Address(ex_mem_1_p17), .WriteEnable(or_2_out), .WriteData(multiplexer_14_out),
    .ReadFromMem(cache_1_readfrommem), .ReadData(cache_1_readdata), .HIT(cache_1_hit),
    .AddressOut(cache_1_addressout), .WriteInMemory(cache_1_writeinmemory), .Last_WE(cache_1_last_we),
    .WriteDataOut(cache_1_writedataout), .Last_W_Data(cache_1_last_w_data));
  memDelayed memdelayed_1 (
    .MemAddress(cache_1_addressout), .MemWriteMask(bit_extender_5_out), .MemWriteData(cache_1_writedataout),
    .clk(clk), .MemReadData(MemData));
  and and_7 (and_7_out, CAcc_EXMEM, not_2_out);
  not not_2 (not_2_out, cache_1_hit);
  Multiplexer #(.select(2), .width(8)) multiplexer_16 (
    .in0(undriven_2[7:0]), .in1(undriven_2[15:8]), .in2(undriven_2[23:16]), .in3(undriven_2[31:24]),
    .out(multiplexer_16_out), .sel(undriven));
  nineClockHolder nineclockholder_1 (.inHold(and_7_out), .clock(clk), .outHold(FRZ));
  Multiplexer #(.width(32)) multiplexer_17 (
    .in0(undriven_2), .in1(bit_extender_6_out), .out(multiplexer_17_out), .sel(LB));
  assign bit_extender_6_out = {{24{1'b1}}, multiplexer_16_out};  // Bit_Extender bit_extender_6
  MEM_WB mem_wb_1 (
    .Clock(clk), .CacheReadDataIn(cache_1_readdata), .MemToRegIn(ex_mem_1_p22), .JumpIn(Jump_EXMEM),
    .RegDstIn(ex_mem_1_p23), .RegWrEnIn(ex_mem_1_p24), .ALU_RES(AluRes_EXMEM), .WrIdxIn(ex_mem_1_p26),
    .PCIN(PC_EXMEM), .SyscalIN(Syscall_EXMEM), .JRIN(JR_EXMEM), .Freeze(FRZ),
    .CacheReadOut(mem_wb_1_cachereadout), .MemToRegOut(memToReg), .JumpOut(Jump_WB), .RegDstOut(RegDst_WB),
    .RegWrEnOut(RegWrEn_WB), .AluRes_WB(AluRes_WB), .WrIdxOut(WrIdx_WB), .PCOUT(PC_WB),
    .SyscallOut(Syscall_WB), .JROUT(JR_WB));
  Multiplexer #(.width(32)) multiplexer_18 (
    .in0(AluRes_WB), .in1(mem_wb_1_cachereadout), .out(multiplexer_18_out), .sel(memToReg));
endmodule
