// Logisim project one_clock_delay.circ as structural Verilog: 1 circuit, main circuit oneClockDelay
module oneClockDelay (
  input  [31:0] DataIn,
  input  clk,
  input  Freeze,
  output [31:0] DataOut
);

  wire xor_1_out;

  xor xor_1 (xor_1_out, 1'b1, Freeze);
  Register #(.width(32)) register_1 (.D(DataIn), .en(xor_1_out), .clk(clk), .Q(DataOut));  // open: clr
endmodule
